// Logisim project CPU.circ as structural Verilog: 1 circuit, main circuit main
module main (
);

  wire undriven_2, undriven_4, undriven_5;
  wire [1:0] undriven_3, undriven_6, undriven_7;
  wire [2:0] undriven_8;
  wire [3:0] alu_proc_1_out_6, multiplexer_1_out, regfile_1_xout, regfile_1_yout, undriven;

  Multiplexer #(.width(4), .enable("false")) multiplexer_1 (
    .in0(alu_proc_1_out_6), .in1(undriven), .out(multiplexer_1_out), .sel(undriven_2));
  // CU_main main_1: pin names not known
  RegFile regfile_1 (
    .RegSel(undriven_3), .XOut(regfile_1_xout), .YOut(regfile_1_yout), .Write(undriven_5), .Read(undriven_4),
    .Din(multiplexer_1_out), .Xsel(undriven_6), .Ysel(undriven_7));
  ALU_PROC alu_proc_1 (
    .S(undriven_8), .in_1(regfile_1_xout), .in_2(regfile_1_yout), .out_6(alu_proc_1_out_6));  // open: Ci, Co
endmodule
