// Logisim project REGISTER.circ as structural Verilog
module REGISTER_4_bits (
  input  [3:0] BUS_R,
  input  CLK,
  input  [3:0] wA,
  input  [3:0] rA1,
  input  [3:0] rA2,
  output [3:0] BUS_Y,
  output [3:0] BUS_X
);

  wire controlled_buffer_1_out, controlled_buffer_2_out, controlled_buffer_3_out, controlled_buffer_4_out,
       flip_flop_d_1_s, flip_flop_d_2_s, flip_flop_d_3_s, flip_flop_d_4_s;

  assign controlled_buffer_1_out = wA[2] ? BUS_R[2] : 1'bz;  // Controlled_Buffer controlled_buffer_1
  assign controlled_buffer_2_out = wA[3] ? BUS_R[3] : 1'bz;  // Controlled_Buffer controlled_buffer_2
  assign controlled_buffer_3_out = wA[0] ? BUS_R[0] : 1'bz;  // Controlled_Buffer controlled_buffer_3
  assign controlled_buffer_4_out = wA[1] ? BUS_R[1] : 1'bz;  // Controlled_Buffer controlled_buffer_4
  FLIP_FLOP_D flip_flop_d_1 (.S(flip_flop_d_1_s), .D(controlled_buffer_3_out), .CLK(CLK));
  FLIP_FLOP_D flip_flop_d_2 (.S(flip_flop_d_2_s), .D(controlled_buffer_4_out), .CLK(CLK));
  FLIP_FLOP_D flip_flop_d_3 (.S(flip_flop_d_3_s), .D(controlled_buffer_1_out), .CLK(CLK));
  FLIP_FLOP_D flip_flop_d_4 (.S(flip_flop_d_4_s), .D(controlled_buffer_2_out), .CLK(CLK));
  assign BUS_X[0] = rA1[3] ? flip_flop_d_1_s : 1'bz;  // Controlled_Buffer controlled_buffer_5
  assign BUS_X[1] = rA1[2] ? flip_flop_d_2_s : 1'bz;  // Controlled_Buffer controlled_buffer_6
  assign BUS_X[2] = rA1[1] ? flip_flop_d_3_s : 1'bz;  // Controlled_Buffer controlled_buffer_7
  assign BUS_X[3] = rA1[0] ? flip_flop_d_4_s : 1'bz;  // Controlled_Buffer controlled_buffer_8
  assign BUS_Y[0] = rA2[3] ? flip_flop_d_1_s : 1'bz;  // Controlled_Buffer controlled_buffer_9
  assign BUS_Y[1] = rA2[2] ? flip_flop_d_2_s : 1'bz;  // Controlled_Buffer controlled_buffer_10
  assign BUS_Y[2] = rA2[1] ? flip_flop_d_3_s : 1'bz;  // Controlled_Buffer controlled_buffer_11
  assign BUS_Y[3] = rA2[0] ? flip_flop_d_4_s : 1'bz;  // Controlled_Buffer controlled_buffer_12
endmodule
